# Fritzing sketch fritzing-led-sketch (saved by Fritzing 1.0.5)
breadboards: 1

parts:
  LED1 = LED - 5mm [color="Red (633nm)" current=0.030A package="5 mm [THT]"]
  VCC1 = Battery [internal_resistance=0.1Ω]
  R1 = Resistor [tolerance=±5% power=0.25W resistance=22 package=THT]
  VM1 = Multimeter (DC Voltage)
  AM1 = Multimeter (DC Current)

nets:
  N1: LED1.cathode, VCC1.-, VM1.COM_Probe
  N2: LED1.anode, R1.Pin_0, VM1.V_Probe
  N3: VCC1.+, AM1.A_Probe
  N4: R1.Pin_1, AM1.COM_Probe

notes:
  Обратите внимание, как меняется яркость светодиода при изменении напряжения батареи или сопротивления резистора.
  Будьте осторожны, стандартный светодиод выдерживает ток не более 30 мА. Если через светодиод протекает больший ток, он выйдет из строя!
  Нажмите кнопку «Начать симуляцию», чтобы запустить симулятор. Он будет имитировать вашу схему при изменении параметров схемы. Чтобы остановить симулятор, нажмите кнопку «Остановить симулятор».
  Схема подключения светодиода, в которой измеряется сила электрического тока, протекающего через светодиод, и падение напряжения на светодиоде.
